# Fritzing sketch data_logger_circuit_diagram (saved by Fritzing 0.9.3b)
breadboards: 1

parts:
  Part1 = Arduino Uno (Rev3)
  ResetBtn = Pushbutton [package="[SMD]"]
  LED1 = LED - 5mm [color="Red (633nm)" package="5 mm [THT]"]  # not connected
  LED2 = LED - 5mm [color="Green (555nm)" package="5 mm [THT]"]  # not connected
  SwitchScreenBtn = Pushbutton [package="[THT]"]
  BacklightBtn = Pushbutton [package="[THT]"]
  PowerLED = LED - 5mm [color="Green (555nm)" package="5 mm [THT]"]  # not connected
  LCD1 = LCD screen  # not connected
  Part2 = Real Time Clock Module - DS1307 RTC Breakout Board
  LED3 = LED - 5mm [color="Red (633nm)" package="5 mm [THT]"]  # not connected
  R1 = Resistor [tolerance=±2% resistance=10k package="1206 [SMD]"]  # not connected

nets:
  5V: Part1.5V, ResetBtn.Pin_3, ResetBtn.Pin_4, Part2.5V
  GND: Part1.GND, SwitchScreenBtn.Pin_3, SwitchScreenBtn.Pin_4, BacklightBtn.Pin_3, BacklightBtn.Pin_4, Part2.GND
  N1: ResetBtn.Pin_1, ResetBtn.Pin_2
  N2: SwitchScreenBtn.Pin_1, SwitchScreenBtn.Pin_2
  N3: BacklightBtn.Pin_1, BacklightBtn.Pin_2
